// Logisim project data_path.circ as structural Verilog: 1 circuit, main circuit main
module main (
);

  wire CLK, jalr, pc_src, RegWrite;
  wire [4:0] bit_lower, reg_file_1_p2, reg_file_1_p3, RS1;
  wire [10:0] bit_upper;
  wire [15:0] imm_16bit;
  wire [19:0] pc_inc, pc_next;
  wire [31:0] BusA, BusB, BusW, R0, R1, R2, R3, R4, R5, R6, R7, R8, R9, R10, R11, R12, R13, R14, R15, R16,
       R17, R18, R19, R20, R21, R22, R23, R24, R25, R26, R27, R28, R29, R30, R31, RA;

  Clock clock_1 (.out(CLK));
  // Reg_file reg_file_1: pin names not known; wires that end beside it: RS1, reg_file_1_p2, reg_file_1_p3, CLK, R0, R1, R2, R3, R4, RegWrite, R5, R6, R7, R8, R9, R10, R11, BusW, R12, R13, R14, R15, R16, R17, R18, R19, R20, R21, R22, R23, R24, R25, R26, R27, R28, R29, R30, R31, BusA, BusB
  // pc_circut_main main_1: pin names not known; wires that end beside it: imm_16bit, bit_upper, bit_lower, RA, CLK, pc_src, jalr, pc_next, pc_inc
endmodule
